// Logisim project Cache.circ as structural Verilog: 5 circuits, main circuit main
module main (
);

  wire controle_cache_1_cachestatus;

  MP MP ();  // open: inputData, store, address, outputData, outputData_2, outputData_3, outputData_4
  Controle_cache controle_cache_1 (
    .store(controle_cache_1_cachestatus), .cacheStatus(controle_cache_1_cachestatus));  // open: in_1, tag
  Cache CACHE (.store(controle_cache_1_cachestatus));  // open: input1, input2, input3, input4, row, tag, word
endmodule

module MP (
  input  [15:0] inputData,
  input  store,
  input  [9:0] address,
  output [15:0] outputData,
  output [15:0] outputData_2,
  output [15:0] outputData_3,
  output [15:0] outputData_4
);

  wire CLK, demultiplexer_1_out0, demultiplexer_1_out1, demultiplexer_1_out2, demultiplexer_1_out3,
       not_1_out, not_2_out, not_3_out, not_4_out;

  Clock clock_1 (.out(CLK));
  Demultiplexer #(.select(2), .enable("false")) demultiplexer_1 (
    .out0(demultiplexer_1_out0), .out1(demultiplexer_1_out1), .out2(demultiplexer_1_out2),
    .out3(demultiplexer_1_out3), .in(store), .sel(address[1:0]));
  assign outputData = demultiplexer_1_out0 ? inputData : 16'bz;  // Controlled_Buffer controlled_buffer_1
  assign outputData_2 = demultiplexer_1_out1 ? inputData : 16'bz;  // Controlled_Buffer controlled_buffer_2
  assign outputData_3 = demultiplexer_1_out2 ? inputData : 16'bz;  // Controlled_Buffer controlled_buffer_3
  assign outputData_4 = demultiplexer_1_out3 ? inputData : 16'bz;  // Controlled_Buffer controlled_buffer_4
  not not_1 (not_1_out, demultiplexer_1_out0);
  not not_2 (not_2_out, demultiplexer_1_out1);
  not not_3 (not_3_out, demultiplexer_1_out2);
  not not_4 (not_4_out, demultiplexer_1_out3);
  RAM #(.dataWidth(16)) ram_1 (.addr(address[9:2]), .data(outputData), .clk(CLK), .ld(not_1_out));  // open: sel, clr
  RAM #(.dataWidth(16)) ram_2 (.addr(address[9:2]), .data(outputData_2), .clk(CLK), .ld(not_2_out));  // open: sel, clr
  RAM #(.dataWidth(16)) ram_3 (.addr(address[9:2]), .data(outputData_3), .clk(CLK), .ld(not_3_out));  // open: sel, clr
  RAM #(.dataWidth(16)) ram_4 (.addr(address[9:2]), .data(outputData_4), .clk(CLK), .ld(not_4_out));  // open: sel, clr
endmodule

module Linha (
  input  [15:0] inputData1,
  input  [15:0] inputData2,
  input  [15:0] inputData3,
  input  store,
  input  [1:0] word,
  input  [15:0] inputData4,
  output [15:0] \output 
);

  wire CLK;
  wire [15:0] output1, output2, output3, output4;

  Clock clock_1 (.out(CLK));
  Register #(.width(16)) register_1 (.D(inputData1), .en(store), .Q(output1), .clk(CLK));  // open: clr
  Register #(.width(16)) register_2 (.D(inputData2), .en(store), .Q(output2), .clk(CLK));  // open: clr
  Register #(.width(16)) register_3 (.D(inputData3), .en(store), .Q(output3), .clk(CLK));  // open: clr
  Register #(.width(16)) register_4 (.D(inputData4), .en(store), .Q(output4), .clk(CLK));  // open: clr
  Multiplexer #(.select(2), .width(16), .enable("false")) multiplexer_1 (
    .in0(output1), .in1(output2), .in2(output3), .in3(output4), .out(\output ), .sel(word));
endmodule

module Cache (
  input  [15:0] input1,
  input  [15:0] input2,
  input  [15:0] input3,
  input  [15:0] input4,
  input  [2:0] row,
  input  [7:0] tag,
  input  [1:0] word,
  input  store
);

  wire row1, row2, row3, row4, row5, row6, row7, row8;

  Demultiplexer #(.select(3), .enable("false")) demultiplexer_1 (
    .out0(row1), .out1(row2), .out2(row3), .out3(row4), .out4(row5), .out5(row6), .out6(row7), .out7(row8),
    .in(store), .sel(row));
  Linha linha_1 (
    .inputData1(input1), .inputData2(input2), .inputData3(input3), .store(row1), .word(word),
    .inputData4(input4));  // open: output
  Linha linha_2 (
    .inputData1(input1), .inputData2(input2), .inputData3(input3), .store(row2), .word(word),
    .inputData4(input4));  // open: output
  Linha linha_3 (
    .inputData1(input1), .inputData2(input2), .inputData3(input3), .store(row3), .word(word),
    .inputData4(input4));  // open: output
  Linha linha_4 (
    .inputData1(input1), .inputData2(input2), .inputData3(input3), .store(row4), .word(word),
    .inputData4(input4));  // open: output
  Linha linha_5 (
    .inputData1(input1), .inputData2(input2), .inputData3(input3), .store(row5), .word(word),
    .inputData4(input4));  // open: output
  Linha linha_6 (
    .inputData1(input1), .inputData2(input2), .inputData3(input3), .store(row6), .word(word),
    .inputData4(input4));  // open: output
  Linha linha_7 (
    .inputData1(input1), .inputData2(input2), .inputData3(input3), .store(row7), .word(word),
    .inputData4(input4));  // open: output
  Linha linha_8 (
    .inputData1(input1), .inputData2(input2), .inputData3(input3), .store(row8), .word(word),
    .inputData4(input4));  // open: output

  // Other names for the same wires on the sheet: word1[15:0] = input1; word2[15:0] = input2; word3[15:0] = input3;
  //   word4[15:0] = input4
endmodule

module Controle_cache (
  input  in_1,
  input  store,
  input  [7:0] tag,
  output cacheStatus
);

  wire CLK, controlled_buffer_1_out, not_1_out;

  Multiplexer multiplexer_1 ();  // open: in0, in1, out, sel, en
  Clock clock_1 (.out(CLK));
  assign controlled_buffer_1_out = store ? in_1 : 1'bz;  // Controlled_Buffer controlled_buffer_1
  not not_1 (not_1_out, store);
  RAM #(.dataWidth(1)) ram_1 (.addr(tag), .data(controlled_buffer_1_out), .clk(CLK), .ld(not_1_out));  // open: sel, clr
  Comparator #(.width(1)) comparator_1 (.a(controlled_buffer_1_out), .b(1'b0), .eq(cacheStatus));  // open: gt, lt
endmodule
